// Logisim project logic_gates.circ as structural Verilog: 1 circuit, main circuit main
module main (
  input  A,
  input  B,
  output AND,
  output OR,
  output NOT
);

  and and_1 (AND, A, B);
  or or_1 (OR, A, B);
  not not_1 (NOT, A);
endmodule
