// Logisim project deselector14.circ as structural Verilog: 1 circuit, main circuit main
module main (
  input  C,
  input  S1,
  input  S0,
  output Z0,
  output Z1,
  output Z2,
  output Z3
);

  wire not_1_out, not_2_out, not_3_out, not_4_out;

  not not_1 (not_1_out, S0);
  not not_2 (not_2_out, S1);
  not not_3 (not_3_out, S1);
  not not_4 (not_4_out, S0);
  or or_1 (Z0, S1, S0, C);
  or or_2 (Z1, S1, not_1_out, C);
  or or_3 (Z2, C, not_2_out, S0);
  or or_4 (Z3, C, not_3_out, not_4_out);
endmodule
