// Logisim project selector41_4bit.circ as structural Verilog: 1 circuit, main circuit main
module main (
  input  [3:0] C0,
  input  [3:0] C1,
  input  [3:0] C2,
  input  [3:0] C3,
  input  S1,
  input  S0,
  output [3:0] Z
);

  wire [3:0] and_1_out, and_2_out, and_3_out, and_4_out, bit_extender_1_out, bit_extender_2_out, not_1_out,
       not_2_out, not_3_out, not_4_out;

  assign bit_extender_1_out = {{3{S1}}, S1};  // Bit_Extender bit_extender_1
  assign bit_extender_2_out = {{3{S0}}, S0};  // Bit_Extender bit_extender_2
  assign not_1_out = ~bit_extender_1_out;  // NOT_Gate not_1, 4 bits wide
  assign not_2_out = ~bit_extender_2_out;  // NOT_Gate not_2, 4 bits wide
  assign not_3_out = ~bit_extender_1_out;  // NOT_Gate not_3, 4 bits wide
  assign not_4_out = ~bit_extender_2_out;  // NOT_Gate not_4, 4 bits wide
  assign and_1_out = not_1_out & not_2_out & C0;  // AND_Gate and_1, 4 bits wide
  assign and_2_out = not_3_out & bit_extender_2_out & C1;  // AND_Gate and_2, 4 bits wide
  assign and_3_out = C2 & bit_extender_1_out & not_4_out;  // AND_Gate and_3, 4 bits wide
  assign and_4_out = C3 & bit_extender_1_out & bit_extender_2_out;  // AND_Gate and_4, 4 bits wide
  assign Z = and_1_out | and_2_out | and_3_out | and_4_out;  // OR_Gate or_1, 4 bits wide
endmodule
