// Logisim project transmission8.circ as structural Verilog: 3 circuits, main circuit main
module main (
  input  D0,
  input  D1,
  input  D2,
  input  D3,
  input  D4,
  input  D5,
  input  D6,
  input  D7,
  input  in_9,
  input  in_10,
  input  in_11,
  output f0,
  output f1,
  output f2,
  output f3,
  output f4,
  output f5,
  output f6,
  output f7
);

  wire and_1_out, and_2_out, not_1_out, not_2_out, or_1_out, or_2_out, or_3_out, selector_1_z, selector_2_z;

  Selector selector_1 (.C0(D0), .C1(D1), .C2(D2), .C3(D3), .S1(in_10), .S0(in_11), .Z(selector_1_z));
  Selector selector_2 (.C0(D4), .C1(D5), .C2(D6), .C3(D7), .S1(in_10), .S0(in_11), .Z(selector_2_z));
  not not_1 (not_1_out, in_9);
  and and_1 (and_1_out, not_1_out, selector_1_z);
  and and_2 (and_2_out, in_9, selector_2_z);
  or or_1 (or_1_out, and_1_out, and_2_out);
  or or_2 (or_2_out, or_1_out, in_9);
  or or_3 (or_3_out, or_1_out, not_2_out);
  not not_2 (not_2_out, in_9);
  DeSelector deselector_1 (.C(or_2_out), .S1(in_10), .S0(in_11), .Z0(f0), .Z1(f1), .Z2(f2), .Z3(f3));
  DeSelector deselector_2 (.C(or_3_out), .S1(in_10), .S0(in_11), .Z0(f4), .Z1(f5), .Z2(f6), .Z3(f7));

  // Notes on the sheet:
  //   A        B       C
  //   MUX
  //   DMUX
endmodule

module Selector (
  input  C0,
  input  C1,
  input  C2,
  input  C3,
  input  S1,
  input  S0,
  output Z
);

  wire and_1_out, and_2_out, and_3_out, and_4_out, not_1_out, not_2_out, not_3_out, not_4_out;

  not not_1 (not_1_out, S1);
  not not_2 (not_2_out, S0);
  not not_3 (not_3_out, S1);
  not not_4 (not_4_out, S0);
  and and_1 (and_1_out, not_1_out, not_2_out, C0);
  and and_2 (and_2_out, not_3_out, S0, C1);
  and and_3 (and_3_out, C2, S1, not_4_out);
  and and_4 (and_4_out, C3, S1, S0);
  or or_1 (Z, and_1_out, and_2_out, and_3_out, and_4_out);
endmodule

module DeSelector (
  input  C,
  input  S1,
  input  S0,
  output Z0,
  output Z1,
  output Z2,
  output Z3
);

  wire not_1_out, not_2_out, not_3_out, not_4_out;

  not not_1 (not_1_out, S0);
  not not_2 (not_2_out, S1);
  not not_3 (not_3_out, S1);
  not not_4 (not_4_out, S0);
  or or_1 (Z0, S1, S0, C);
  or or_2 (Z1, S1, not_1_out, C);
  or or_3 (Z2, C, not_2_out, S0);
  or or_4 (Z3, C, not_3_out, not_4_out);
endmodule
