// Logisim project decoder.circ as structural Verilog: 1 circuit, main circuit main
module main (
  input  G1,
  input  G2,
  input  D2,
  input  D1,
  input  D0,
  output out_6,
  output out_7,
  output out_8,
  output out_9,
  output out_10,
  output out_11,
  output out_12,
  output out_13
);

  wire and_1_out, not_1_out, not_2_out, not_3_out, not_4_out, not_5_out, not_6_out, not_7_out;

  not not_1 (not_1_out, G2);
  not not_2 (not_2_out, D2);
  not not_3 (not_3_out, D1);
  not not_4 (not_4_out, D0);
  and and_1 (and_1_out, G1, not_1_out);
  not not_5 (not_5_out, not_2_out);
  not not_6 (not_6_out, not_3_out);
  not not_7 (not_7_out, not_4_out);
  nand nand_1 (out_6, not_2_out, not_3_out, not_4_out, and_1_out);
  nand nand_2 (out_7, not_5_out, not_3_out, not_4_out, and_1_out);
  nand nand_3 (out_8, not_2_out, not_6_out, not_4_out, and_1_out);
  nand nand_4 (out_9, not_5_out, not_6_out, not_4_out, and_1_out);
  nand nand_5 (out_10, not_2_out, not_3_out, not_7_out, and_1_out);
  nand nand_6 (out_11, not_3_out, not_7_out, not_5_out, and_1_out);
  nand nand_7 (out_12, not_2_out, not_7_out, not_6_out, and_1_out);
  nand nand_8 (out_13, and_1_out, not_6_out, not_7_out, not_5_out);
endmodule
