// Logisim project encoder83.circ as structural Verilog: 1 circuit, main circuit main
module main (
  input  D0,
  input  D1,
  input  D2,
  input  D3,
  input  D4,
  input  D5,
  input  D6,
  input  D7,
  output Y0,
  output Y1,
  output Y2
);

  or or_1 (Y0, D1, D3, D5, D7);
  or or_2 (Y1, D2, D3, D6, D7);
  or or_3 (Y2, D4, D5, D6, D7);
endmodule
