// Logisim project 多路选择器型-加法器.circ as structural Verilog: 1 circuit, main circuit main
module main (
  input  [7:0] in_1,
  output out_2
);

  wire adder_1_cout, and_1_out, and_2_out, and_3_out, and_4_out, and_5_out, clock_1_out, d_ff_1_qn,
       d_ff_2_qn, multiplexer_1_out, multiplexer_2_out, nor_1_out, not_1_out, or_1_out, xor_1_out, xor_2_out;
  wire [1:0] d_ff_2_q;
  wire [7:0] adder_1_out, controlled_buffer_1_out, register_1_q, register_2_q;

  Multiplexer #(.select(2)) multiplexer_1 (
    .in0(1'b0), .in1(1'b1), .in2(1'b1), .in3(1'b1), .out(multiplexer_1_out), .sel(d_ff_2_q));  // open: en
  Multiplexer #(.select(2)) multiplexer_2 (
    .in0(1'b1), .in1(1'b1), .in2(1'b1), .in3(1'b0), .out(multiplexer_2_out), .sel(d_ff_2_q));  // open: en
  Clock clock_1 (.out(clock_1_out));
  not not_1 (not_1_out, clock_1_out);
  D_Flip_Flop d_ff_1 (
    .clk(clock_1_out), .D(multiplexer_1_out), .Q(d_ff_2_q[1]), .Qn(d_ff_1_qn));  // open: preset, en, reset
  D_Flip_Flop d_ff_2 (
    .clk(clock_1_out), .D(multiplexer_2_out), .Q(d_ff_2_q[0]), .Qn(d_ff_2_qn));  // open: preset, en, reset
  and and_1 (and_1_out, d_ff_2_q[1], d_ff_2_q[0]);
  and and_2 (and_2_out, d_ff_1_qn, d_ff_2_qn);
  or or_1 (or_1_out, and_1_out, and_2_out);
  xor xor_1 (xor_1_out, d_ff_2_q[1], d_ff_2_q[0]);
  xor xor_2 (xor_2_out, d_ff_2_q[1], d_ff_2_q[0]);
  nor nor_1 (nor_1_out, d_ff_2_q[1], d_ff_2_q[0]);
  and and_3 (and_3_out, or_1_out, not_1_out);
  and and_4 (and_4_out, xor_1_out, not_1_out);
  Register register_1 (.D(in_1), .Q(register_1_q), .clk(and_3_out));  // open: en, clr
  Register register_2 (.D(adder_1_out), .Q(register_2_q), .clk(and_4_out));  // open: en, clr
  and and_5 (and_5_out, xor_2_out, not_1_out);
  assign controlled_buffer_1_out = xor_2_out ? register_2_q : 8'bz;  // Controlled_Buffer controlled_buffer_1
  Register #(.width(1)) register_3 (.D(adder_1_cout), .Q(out_2), .clk(and_5_out), .clr(nor_1_out));  // open: en
  Adder adder_1 (.a(register_1_q), .b(controlled_buffer_1_out), .out(adder_1_out), .cout(adder_1_cout));  // open: cin

  // Notes on the sheet:
  //   B
  //   A
  //   T1
  //   T2
  //   LDA
  //   LDB
  //   ADD
  //   ___
  //   CLR
endmodule
