// Logisim project 定序型_加法器.circ as structural Verilog: 1 circuit, main circuit main
module main (
  input  [7:0] in_1,
  output out_2
);

  wire adder_1_cout, and_1_out, and_2_out, and_3_out, clock_1_out, d_ff_1_q, d_ff_2_q, d_ff_3_q, d_ff_4_q,
       nor_1_out, not_1_out, or_1_out, or_2_out, xor_1_out, xor_2_out;
  wire [7:0] adder_1_out, controlled_buffer_1_out, register_1_q, register_2_q;

  nor nor_1 (nor_1_out, d_ff_1_q, d_ff_2_q, d_ff_3_q, d_ff_4_q);
  or or_1 (or_1_out, d_ff_2_q, d_ff_4_q);
  not not_1 (not_1_out, clock_1_out);
  Clock clock_1 (.out(clock_1_out));
  D_Flip_Flop d_ff_1 (.clk(clock_1_out), .D(nor_1_out), .Q(d_ff_1_q));  // open: Qn, preset, en, reset
  D_Flip_Flop d_ff_2 (.clk(clock_1_out), .D(d_ff_1_q), .Q(d_ff_2_q));  // open: Qn, preset, en, reset
  D_Flip_Flop d_ff_3 (.clk(clock_1_out), .D(or_1_out), .Q(d_ff_3_q));  // open: Qn, preset, en, reset
  D_Flip_Flop d_ff_4 (.clk(clock_1_out), .D(d_ff_3_q), .Q(d_ff_4_q));  // open: Qn, preset, en, reset
  or or_2 (or_2_out, d_ff_1_q, d_ff_3_q);
  xor xor_1 (xor_1_out, d_ff_2_q, d_ff_4_q);
  xor xor_2 (xor_2_out, d_ff_2_q, d_ff_4_q);
  and and_1 (and_1_out, or_2_out, not_1_out);
  and and_2 (and_2_out, xor_1_out, not_1_out);
  Register register_1 (.D(in_1), .Q(register_1_q), .clk(and_1_out));  // open: en, clr
  Register register_2 (.D(adder_1_out), .Q(register_2_q), .clk(and_2_out));  // open: en, clr
  and and_3 (and_3_out, xor_2_out, not_1_out);
  assign controlled_buffer_1_out = xor_2_out ? register_2_q : 8'bz;  // Controlled_Buffer controlled_buffer_1
  Register #(.width(1)) register_3 (.D(adder_1_cout), .Q(out_2), .clk(and_3_out), .clr(d_ff_1_q));  // open: en
  Adder adder_1 (.a(register_1_q), .b(controlled_buffer_1_out), .out(adder_1_out), .cout(adder_1_cout));  // open: cin

  // Notes on the sheet:
  //   T1
  //   T2
  //   LDA
  //   LDB
  //   ADD
  //   ___
  //   CLR
endmodule
