// Logisim project 定序型_比较器.circ as structural Verilog: 1 circuit, main circuit main
module main (
  input  [7:0] in_1
);

  wire and_1_out, and_2_out, and_3_out, and_4_out, clock_1_out, comparator_1_gt, d_ff_1_q, d_ff_2_q,
       d_ff_3_q, d_ff_4_q, nor_1_out, not_1_out, not_2_out, or_1_out, or_2_out, or_3_out;
  wire [7:0] controlled_buffer_1_out, controlled_buffer_2_out, register_1_q, register_2_q;

  and and_1 (and_1_out, not_2_out, d_ff_4_q);
  and and_2 (and_2_out, comparator_1_gt, d_ff_4_q);
  nor nor_1 (nor_1_out, d_ff_1_q, d_ff_2_q, d_ff_3_q, d_ff_4_q);
  or or_1 (or_1_out, and_1_out, d_ff_1_q);
  or or_2 (or_2_out, and_2_out, d_ff_2_q);
  Clock clock_1 (.out(clock_1_out));
  D_Flip_Flop d_ff_1 (.clk(clock_1_out), .D(nor_1_out), .Q(d_ff_1_q));  // open: Qn, preset, en, reset
  D_Flip_Flop d_ff_2 (.clk(clock_1_out), .D(or_1_out), .Q(d_ff_2_q));  // open: Qn, preset, en, reset
  D_Flip_Flop d_ff_3 (.clk(clock_1_out), .D(or_2_out), .Q(d_ff_3_q));  // open: Qn, preset, en, reset
  D_Flip_Flop d_ff_4 (.clk(clock_1_out), .D(d_ff_3_q), .Q(d_ff_4_q));  // open: Qn, preset, en, reset
  not not_1 (not_1_out, clock_1_out);
  or or_3 (or_3_out, d_ff_1_q, d_ff_3_q);
  and and_3 (and_3_out, d_ff_2_q, not_1_out);
  and and_4 (and_4_out, or_3_out, not_1_out);
  Register register_1 (.D(register_2_q), .Q(register_1_q), .clk(and_3_out));  // open: en, clr
  assign controlled_buffer_1_out = d_ff_4_q ? register_1_q : 8'bz;  // Controlled_Buffer controlled_buffer_1
  assign controlled_buffer_2_out = d_ff_4_q ? register_2_q : 8'bz;  // Controlled_Buffer controlled_buffer_2
  Register register_2 (.D(in_1), .Q(register_2_q), .clk(and_4_out));  // open: en, clr
  not not_2 (not_2_out, comparator_1_gt);
  Comparator comparator_1 (
    .a(controlled_buffer_1_out), .b(controlled_buffer_2_out), .gt(comparator_1_gt));  // open: eq, lt

  // Notes on the sheet:
  //   T1
  //   INPUT
  //   T2
  //   LDA
  //   LDB
  //   CAP
endmodule
