// Logisim project 计数器型_比较器.circ as structural Verilog: 1 circuit, main circuit main
module main (
  input  [7:0] in_1
);

  wire and_1_out, and_2_out, and_3_out, and_4_out, and_5_out, clock_1_out, comparator_1_gt, d_ff_1_q,
       d_ff_1_qn, d_ff_2_q, d_ff_2_qn, not_1_out, or_1_out, or_2_out, xnor_1_out;
  wire [7:0] controlled_buffer_1_out, controlled_buffer_2_out, register_1_q, register_2_q;

  and and_1 (and_1_out, comparator_1_gt, d_ff_2_qn, d_ff_1_q);
  or or_1 (or_1_out, d_ff_2_qn, d_ff_1_qn);
  Clock clock_1 (.out(clock_1_out));
  D_Flip_Flop d_ff_1 (.clk(clock_1_out), .D(or_2_out), .Q(d_ff_1_q), .Qn(d_ff_1_qn));  // open: preset, en, reset
  or or_2 (or_2_out, and_1_out, d_ff_2_q);
  D_Flip_Flop d_ff_2 (.clk(clock_1_out), .D(or_1_out), .Q(d_ff_2_q), .Qn(d_ff_2_qn));  // open: preset, en, reset
  not not_1 (not_1_out, clock_1_out);
  and and_2 (and_2_out, d_ff_2_q, d_ff_1_qn);
  xnor xnor_1 (xnor_1_out, d_ff_2_q, d_ff_1_q);
  and and_3 (and_3_out, d_ff_1_q, d_ff_2_qn);
  and and_4 (and_4_out, and_2_out, not_1_out);
  and and_5 (and_5_out, xnor_1_out, not_1_out);
  Register register_1 (.D(register_2_q), .Q(register_1_q), .clk(and_4_out));  // open: en, clr
  assign controlled_buffer_1_out = and_3_out ? register_1_q : 8'bz;  // Controlled_Buffer controlled_buffer_1
  assign controlled_buffer_2_out = and_3_out ? register_2_q : 8'bz;  // Controlled_Buffer controlled_buffer_2
  Register register_2 (.D(in_1), .Q(register_2_q), .clk(and_5_out));  // open: en, clr
  Comparator comparator_1 (
    .a(controlled_buffer_1_out), .b(controlled_buffer_2_out), .gt(comparator_1_gt));  // open: eq, lt

  // Notes on the sheet:
  //   B
  //   A
  //   T1
  //   T2
  //   INPUT
  //   LDA
  //   LDB
  //   CAP
endmodule
